# Fritzing sketch Alchemy room controller schematic (saved by Fritzing 1.0.0rc)
breadboards: 1

parts:
  A1 = Particle - Photon2
  OLED_I2C1 = OLED 128x64 I2C Monochrome Display
  M1 = BMP280
  Grove_Ultrasonic_Ranger1 = Grove Ultrasonic Ranger
  Part1 = 16 NeoPixel Ring [part_number=1463]
  U1 = ENCODER_RGB [package=encoder_led_2]

nets:
  VDD: A1.Pin_2, OLED_I2C1.VDD, M1.VIN, Grove_Ultrasonic_Ranger1.VCC
  GND: A1.Pin_4, A1.Pin_30, OLED_I2C1.GND, M1.GND, Grove_Ultrasonic_Ranger1.GND, Part1.GND, U1.C
  N1: A1.Pin_7, Grove_Ultrasonic_Ranger1.SIG
  N2: A1.Pin_9, Grove_Ultrasonic_Ranger1.NC
  N3: A1.Pin_10, U1.R
  N4: A1.Pin_11, U1.G
  N5: A1.Pin_12, U1.SW
  N6: A1.Pin_13, U1.B#8
  N7: A1.Pin_14, U1.A
  N8: A1.Pin_15, U1.B#2
  N9: A1.Pin_17, OLED_I2C1.SDA, M1.SDA
  N10: A1.Pin_18, OLED_I2C1.SCK, M1.SCL
  N11: A1.Pin_19, Part1.IN
  N12: A1.Pin_26, Part1.VDD

custom parts:
  Particle - Photon2: The Photon 2 is a microcontroller and Wi-Fi networking developed by particle. Features: 802.11a/b/g/n Wi-Fi, 2.4 GHz and 5 GHz Integrated PCB antenna Integrated U.FL connector for external antenna Integrated RF switch BLE 5 using same antenna as Wi-Fi Realtek RTL8721DM MCU ARM Cortex M33 CPU, 200 MHz 2048 KB (2 MB) user application maximum size 3072 KB (3 MB) of RAM available to user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
  BMP280: Temperature Humidity Barometric presure Sensor, I2C
  Grove Ultrasonic Ranger: Ultrasonic Ranger, Grove connector.
  16 NeoPixel Ring: 16 ultra bright smart LED NeoPixels are arranged in a circle with 1.75" (44.5mm) outer diameter. The rings are 'chainable' - connect the output pin of one to the input pin of another. Use only one microcontroller pin to control as many as you can chain together! Each LED is addressable as the driver chip is inside the LED. Each one has ~18mA constant current drive so the color will be very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
  ENCODER_RGB: SparkFun RGB rotary Encoder
